// Logisim project decoder_hexa.circ as structural Verilog: 2 circuits, main circuit main
module main (
  input  in_1,
  input  in_2,
  input  in_3,
  input  in_4
);

  wire decoder_4to6_1_y0, decoder_4to6_1_y1, decoder_4to6_1_y2, decoder_4to6_1_y3, decoder_4to6_1_y4,
       decoder_4to6_1_y5, decoder_4to6_1_y6, decoder_4to6_1_y7, decoder_4to6_1_y8, decoder_4to6_1_y9,
       decoder_4to6_1_y10, decoder_4to6_1_y11, decoder_4to6_1_y12, decoder_4to6_1_y13, decoder_4to6_1_y14,
       decoder_4to6_1_y15, OR02_out, OR04_out, OR35_out, OR67_out, OR68_out, OR89_out, OR301_out, or_1_out,
       or_2_out, or_3_out, or_4_out, or_5_out, or_6_out, or_7_out, or_8_out, or_9_out, or_10_out, or_11_out,
       or_12_out, or_13_out, or_14_out, or_15_out, or_16_out, or_17_out, or_18_out, or_19_out, or_20_out,
       or_21_out, or_22_out, or_23_out, or_24_out, or_25_out, or_26_out, or_27_out, or_28_out, or_29_out,
       or_30_out, or_31_out, or_32_out, or_33_out, or_34_out, or_35_out, or_36_out, or_37_out, or_38_out,
       or_39_out, or_40_out, or_41_out, or_42_out, or_43_out, or_44_out, or_45_out, or_46_out, or_47_out,
       or_48_out, or_49_out, or_50_out, or_51_out, or_52_out, or_53_out, or_54_out;

  Decoder_4to6 decoder_4to6_1 (
    .A0(in_1), .A1(in_2), .A2(in_3), .A3(in_4), .Y0(decoder_4to6_1_y0), .Y1(decoder_4to6_1_y1),
    .Y2(decoder_4to6_1_y2), .Y3(decoder_4to6_1_y3), .Y4(decoder_4to6_1_y4), .Y5(decoder_4to6_1_y5),
    .Y6(decoder_4to6_1_y6), .Y7(decoder_4to6_1_y7), .Y8(decoder_4to6_1_y8), .Y9(decoder_4to6_1_y9),
    .Y10(decoder_4to6_1_y10), .Y11(decoder_4to6_1_y11), .Y12(decoder_4to6_1_y12), .Y13(decoder_4to6_1_y13),
    .Y14(decoder_4to6_1_y14), .Y15(decoder_4to6_1_y15));
  or OR02 (OR02_out, decoder_4to6_1_y0, decoder_4to6_1_y2);
  or OR35 (OR35_out, decoder_4to6_1_y3, decoder_4to6_1_y5);
  or OR89 (OR89_out, decoder_4to6_1_y8, decoder_4to6_1_y9);
  or or_1 (or_1_out, decoder_4to6_1_y0, decoder_4to6_1_y1);
  or or_2 (or_2_out, decoder_4to6_1_y4, decoder_4to6_1_y7);
  or OR04 (OR04_out, decoder_4to6_1_y0, decoder_4to6_1_y4);
  or OR67 (OR67_out, decoder_4to6_1_y6, decoder_4to6_1_y7);
  or or_3 (or_3_out, decoder_4to6_1_y0, decoder_4to6_1_y2);
  or OR68 (OR68_out, decoder_4to6_1_y6, decoder_4to6_1_y8);
  or or_4 (or_4_out, decoder_4to6_1_y5, decoder_4to6_1_y6);
  or or_5 (or_5_out, decoder_4to6_1_y2, decoder_4to6_1_y3);
  or or_6 (or_6_out, decoder_4to6_1_y11, decoder_4to6_1_y12);
  or or_7 (or_7_out, decoder_4to6_1_y13, decoder_4to6_1_y14);
  or or_8 (or_8_out, decoder_4to6_1_y10, decoder_4to6_1_y11);
  or or_9 (or_9_out, decoder_4to6_1_y12, decoder_4to6_1_y13);
  or or_10 (or_10_out, decoder_4to6_1_y14, decoder_4to6_1_y15);
  or or_11 (or_11_out, decoder_4to6_1_y12, decoder_4to6_1_y14);
  or or_12 (or_12_out, OR02_out, OR35_out);
  or or_13 (or_13_out, OR67_out, OR89_out);
  or OR301 (OR301_out, decoder_4to6_1_y3, or_1_out);
  or or_14 (or_14_out, OR89_out, or_2_out);
  or or_15 (or_15_out, or_1_out, decoder_4to6_1_y3);
  or or_16 (or_16_out, decoder_4to6_1_y4, decoder_4to6_1_y5);
  or or_17 (or_17_out, OR67_out, OR89_out);
  or or_18 (or_18_out, or_3_out, OR35_out);
  or or_19 (or_19_out, OR68_out, decoder_4to6_1_y9);
  or or_20 (or_20_out, OR02_out, OR68_out);
  or or_21 (or_21_out, OR68_out, OR04_out);
  or or_22 (or_22_out, OR89_out, decoder_4to6_1_y5);
  or or_23 (or_23_out, or_4_out, OR89_out);
  or or_24 (or_24_out, or_5_out, decoder_4to6_1_y4);
  or or_25 (or_25_out, or_32_out, decoder_4to6_1_y10);
  or or_26 (or_26_out, decoder_4to6_1_y12, decoder_4to6_1_y14);
  or or_27 (or_27_out, decoder_4to6_1_y10, decoder_4to6_1_y13);
  or or_28 (or_28_out, decoder_4to6_1_y10, decoder_4to6_1_y11);
  or or_29 (or_29_out, or_6_out, or_7_out);
  or or_30 (or_30_out, or_8_out, or_11_out);
  or or_31 (or_31_out, decoder_4to6_1_y14, decoder_4to6_1_y13);
  or or_32 (or_32_out, or_12_out, or_13_out);
  or or_33 (or_33_out, OR301_out, or_14_out);
  or or_34 (or_34_out, or_15_out, or_16_out);
  or or_35 (or_35_out, or_16_out, or_17_out);
  or or_36 (or_36_out, or_18_out, or_19_out);
  or or_37 (or_37_out, or_21_out, or_22_out);
  or or_38 (or_38_out, or_23_out, or_24_out);
  or or_39 (or_39_out, or_25_out, or_26_out);
  or or_40 (or_40_out, or_28_out, decoder_4to6_1_y13);
  or or_41 (or_41_out, or_8_out, or_9_out);
  _7_Segment_Display u_7_segment_display_1 (
    .g(or_54_out), .f(or_53_out), .a(or_44_out), .b(or_49_out), .e(or_52_out), .d(or_51_out), .c(or_50_out));  // open: dp
  or or_42 (or_42_out, decoder_4to6_1_y2, or_33_out);
  or or_43 (or_43_out, or_34_out, or_35_out);
  or or_44 (or_44_out, or_39_out, decoder_4to6_1_y15);
  or or_45 (or_45_out, or_41_out, or_10_out);
  or or_46 (or_46_out, or_30_out, decoder_4to6_1_y15);
  or or_47 (or_47_out, or_8_out, or_31_out);
  or or_48 (or_48_out, or_47_out, decoder_4to6_1_y15);
  or or_49 (or_49_out, or_42_out, or_27_out);
  or or_50 (or_50_out, or_40_out, or_43_out);
  or or_51 (or_51_out, or_36_out, or_29_out);
  or or_52 (or_52_out, or_20_out, or_45_out);
  or or_53 (or_53_out, or_37_out, or_46_out);
  or or_54 (or_54_out, or_38_out, or_48_out);
endmodule

module Decoder_4to6 (
  input  A0,
  input  A1,
  input  A2,
  input  A3,
  output Y0,
  output Y1,
  output Y2,
  output Y3,
  output Y4,
  output Y5,
  output Y6,
  output Y7,
  output Y8,
  output Y9,
  output Y10,
  output Y11,
  output Y12,
  output Y13,
  output Y14,
  output Y15
);

  wire and_1_out, and_2_out, and_3_out, and_4_out, and_5_out, and_6_out, and_7_out, and_8_out, and_9_out,
       and_10_out, and_11_out, and_12_out, and_13_out, and_14_out, and_15_out, and_16_out, and_17_out,
       and_18_out, and_19_out, and_20_out, and_21_out, and_22_out, and_23_out, and_24_out, and_25_out,
       and_26_out, and_27_out, and_28_out, and_29_out, and_30_out, and_31_out, and_32_out, not_1_out,
       not_2_out, not_3_out, not_4_out, not_5_out, not_6_out, not_7_out, not_8_out, not_9_out, not_10_out,
       not_11_out;

  not not_1 (not_1_out, A0);
  not not_2 (not_2_out, A1);
  not not_3 (not_3_out, A0);
  not not_4 (not_4_out, A1);
  not not_5 (not_5_out, A0);
  not not_6 (not_6_out, A1);
  not not_7 (not_7_out, A0);
  not not_8 (not_8_out, A1);
  and and_1 (and_1_out, not_1_out, not_2_out);
  and and_2 (and_2_out, A0, not_2_out);
  and and_3 (and_3_out, not_1_out, A1);
  and and_4 (and_4_out, A1, A0);
  and and_5 (and_5_out, not_3_out, not_4_out);
  and and_6 (and_6_out, A0, not_4_out);
  and and_7 (and_7_out, not_3_out, A1);
  and and_8 (and_8_out, A1, A0);
  and and_9 (and_9_out, not_5_out, not_6_out);
  and and_10 (and_10_out, A0, not_6_out);
  and and_11 (and_11_out, not_5_out, A1);
  and and_12 (and_12_out, A1, A0);
  and and_13 (and_13_out, not_7_out, not_8_out);
  and and_14 (and_14_out, A0, not_8_out);
  and and_15 (and_15_out, not_7_out, A1);
  and and_16 (and_16_out, A1, A0);
  not not_9 (not_9_out, A2);
  not not_10 (not_10_out, A2);
  and and_17 (and_17_out, and_1_out, not_9_out);
  and and_18 (and_18_out, not_9_out, and_2_out);
  and and_19 (and_19_out, and_3_out, not_9_out);
  and and_20 (and_20_out, and_4_out, not_9_out);
  and and_21 (and_21_out, A2, and_5_out);
  and and_22 (and_22_out, A2, and_6_out);
  and and_23 (and_23_out, A2, and_7_out);
  and and_24 (and_24_out, A2, and_8_out);
  and and_25 (and_25_out, and_9_out, not_10_out);
  and and_26 (and_26_out, not_10_out, and_10_out);
  and and_27 (and_27_out, and_11_out, not_10_out);
  and and_28 (and_28_out, and_12_out, not_10_out);
  and and_29 (and_29_out, A2, and_13_out);
  and and_30 (and_30_out, A2, and_14_out);
  and and_31 (and_31_out, A2, and_15_out);
  and and_32 (and_32_out, A2, and_16_out);
  not not_11 (not_11_out, A3);
  and and_33 (Y0, not_11_out, and_17_out);
  and and_34 (Y1, not_11_out, and_18_out);
  and and_35 (Y2, not_11_out, and_19_out);
  and and_36 (Y3, not_11_out, and_20_out);
  and and_37 (Y4, not_11_out, and_21_out);
  and and_38 (Y5, not_11_out, and_22_out);
  and and_39 (Y6, not_11_out, and_23_out);
  and and_40 (Y7, not_11_out, and_24_out);
  and and_41 (Y8, A3, and_25_out);
  and and_42 (Y9, A3, and_26_out);
  and and_43 (Y10, A3, and_27_out);
  and and_44 (Y11, A3, and_28_out);
  and and_45 (Y12, A3, and_29_out);
  and and_46 (Y13, A3, and_30_out);
  and and_47 (Y14, A3, and_31_out);
  and and_48 (Y15, A3, and_32_out);
endmodule
