// Logisim project encoder_7.circ as structural Verilog: 2 circuits, main circuit main
module main (
  input  A1,
  input  A2,
  input  A3,
  input  A4,
  input  A5,
  input  A6,
  input  A7,
  input  A8,
  input  A9,
  input  A10,
  input  A11,
  input  A12,
  input  A13,
  input  A14,
  input  A15
);

  wire dec_1_y0, dec_1_y1, dec_1_y2, dec_1_y3, dec_1_y4, dec_1_y5, dec_1_y6, dec_1_y7, dec_1_y8, dec_1_y9,
       dec_1_y10, dec_1_y11, dec_1_y12, dec_1_y13, dec_1_y14, dec_1_y15, OR02_out, OR04_out, OR35_out,
       OR67_out, OR68_out, OR89_out, OR301_out, or_1_out, or_2_out, or_3_out, or_4_out, or_5_out, or_6_out,
       or_7_out, or_8_out, or_9_out, or_10_out, or_11_out, or_12_out, or_13_out, or_14_out, or_15_out,
       or_16_out, or_17_out, or_18_out, or_19_out, or_20_out, or_21_out, or_22_out, or_23_out, or_24_out,
       or_25_out, or_26_out, or_27_out, or_28_out, or_29_out, or_30_out, or_31_out, or_32_out, or_33_out,
       or_34_out, or_35_out, or_36_out, or_37_out, or_38_out, or_39_out, or_40_out, or_41_out, or_42_out,
       or_43_out, or_44_out, or_45_out, or_46_out, or_47_out, or_48_out, or_49_out, or_50_out, or_51_out,
       or_52_out, or_53_out, or_54_out, or_55_out, or_56_out, or_57_out, or_58_out, or_59_out, or_60_out,
       or_61_out, or_62_out, or_63_out, or_64_out, or_65_out, or_66_out, or_67_out, or_68_out, or_69_out,
       or_70_out, or_71_out, or_72_out, or_73_out, or_74_out, or_75_out, or_76_out, or_77_out, or_78_out,
       or_79_out, or_80_out, or_81_out, or_82_out;

  or or_1 (or_1_out, A3, A1);
  or or_2 (or_2_out, A5, A7);
  or or_3 (or_3_out, A9, A11);
  or or_4 (or_4_out, A13, A15);
  or or_5 (or_5_out, A2, A3);
  or or_6 (or_6_out, A6, A7);
  or or_7 (or_7_out, A10, A11);
  or or_8 (or_8_out, A14, A15);
  or or_9 (or_9_out, A4, A5);
  or or_10 (or_10_out, A6, A7);
  or or_11 (or_11_out, A12, A13);
  or or_12 (or_12_out, A14, A15);
  or or_13 (or_13_out, A8, A9);
  or or_14 (or_14_out, A10, A11);
  or or_15 (or_15_out, A12, A13);
  or or_16 (or_16_out, A14, A15);
  or or_17 (or_17_out, or_1_out, or_2_out);
  or or_18 (or_18_out, or_3_out, or_4_out);
  or or_19 (or_19_out, or_5_out, or_6_out);
  or or_20 (or_20_out, or_7_out, or_8_out);
  or or_21 (or_21_out, or_9_out, or_10_out);
  or or_22 (or_22_out, or_11_out, or_12_out);
  or or_23 (or_23_out, or_13_out, or_14_out);
  or or_24 (or_24_out, or_15_out, or_16_out);
  or or_25 (or_25_out, or_17_out, or_18_out);
  or or_26 (or_26_out, or_19_out, or_20_out);
  or or_27 (or_27_out, or_21_out, or_22_out);
  or or_28 (or_28_out, or_23_out, or_24_out);
  dec dec_1 (
    .A0(or_25_out), .A1(or_26_out), .A2(or_27_out), .A3(or_28_out), .Y0(dec_1_y0), .Y1(dec_1_y1),
    .Y2(dec_1_y2), .Y3(dec_1_y3), .Y4(dec_1_y4), .Y5(dec_1_y5), .Y6(dec_1_y6), .Y7(dec_1_y7), .Y8(dec_1_y8),
    .Y9(dec_1_y9), .Y10(dec_1_y10), .Y11(dec_1_y11), .Y12(dec_1_y12), .Y13(dec_1_y13), .Y14(dec_1_y14),
    .Y15(dec_1_y15));
  or OR02 (OR02_out, dec_1_y0, dec_1_y2);
  or OR35 (OR35_out, dec_1_y3, dec_1_y5);
  or OR67 (OR67_out, dec_1_y6, dec_1_y7);
  or OR89 (OR89_out, dec_1_y8, dec_1_y9);
  or or_29 (or_29_out, dec_1_y0, dec_1_y1);
  or or_30 (or_30_out, dec_1_y4, dec_1_y7);
  or or_31 (or_31_out, dec_1_y0, dec_1_y2);
  or OR68 (OR68_out, dec_1_y6, dec_1_y8);
  or OR04 (OR04_out, dec_1_y0, dec_1_y4);
  or or_32 (or_32_out, dec_1_y5, dec_1_y6);
  or or_33 (or_33_out, dec_1_y2, dec_1_y3);
  or or_34 (or_34_out, dec_1_y10, dec_1_y11);
  or or_35 (or_35_out, dec_1_y11, dec_1_y12);
  or or_36 (or_36_out, dec_1_y13, dec_1_y14);
  or or_37 (or_37_out, dec_1_y10, dec_1_y11);
  or or_38 (or_38_out, dec_1_y12, dec_1_y13);
  or or_39 (or_39_out, dec_1_y14, dec_1_y15);
  or or_40 (or_40_out, dec_1_y12, dec_1_y14);
  or or_41 (or_41_out, OR02_out, OR35_out);
  or or_42 (or_42_out, OR67_out, OR89_out);
  or OR301 (OR301_out, dec_1_y3, or_29_out);
  or or_43 (or_43_out, OR89_out, or_30_out);
  or or_44 (or_44_out, or_29_out, dec_1_y3);
  or or_45 (or_45_out, dec_1_y4, dec_1_y5);
  or or_46 (or_46_out, OR67_out, OR89_out);
  or or_47 (or_47_out, or_31_out, OR35_out);
  or or_48 (or_48_out, OR68_out, dec_1_y9);
  or or_49 (or_49_out, OR02_out, OR68_out);
  or or_50 (or_50_out, OR68_out, OR04_out);
  or or_51 (or_51_out, OR89_out, dec_1_y5);
  or or_52 (or_52_out, or_32_out, OR89_out);
  or or_53 (or_53_out, or_33_out, dec_1_y4);
  or or_54 (or_54_out, or_60_out, dec_1_y10);
  or or_55 (or_55_out, dec_1_y12, dec_1_y14);
  or or_56 (or_56_out, dec_1_y10, dec_1_y13);
  or or_57 (or_57_out, or_35_out, or_36_out);
  or or_58 (or_58_out, or_37_out, or_40_out);
  or or_59 (or_59_out, dec_1_y14, dec_1_y13);
  or or_60 (or_60_out, or_41_out, or_42_out);
  or or_61 (or_61_out, OR301_out, or_43_out);
  or or_62 (or_62_out, or_44_out, or_45_out);
  or or_63 (or_63_out, or_45_out, or_46_out);
  or or_64 (or_64_out, or_47_out, or_48_out);
  or or_65 (or_65_out, or_50_out, or_51_out);
  or or_66 (or_66_out, or_52_out, or_53_out);
  or or_67 (or_67_out, or_54_out, or_55_out);
  or or_68 (or_68_out, or_34_out, dec_1_y13);
  or or_69 (or_69_out, or_37_out, or_38_out);
  or or_70 (or_70_out, or_58_out, dec_1_y15);
  or or_71 (or_71_out, or_37_out, or_59_out);
  _7_Segment_Display u_7_segment_display_1 (
    .g(or_82_out), .f(or_81_out), .a(or_74_out), .b(or_77_out), .e(or_80_out), .d(or_79_out), .c(or_78_out));  // open: dp
  or or_72 (or_72_out, dec_1_y2, or_61_out);
  or or_73 (or_73_out, or_62_out, or_63_out);
  or or_74 (or_74_out, or_67_out, dec_1_y15);
  or or_75 (or_75_out, or_69_out, or_39_out);
  or or_76 (or_76_out, or_71_out, dec_1_y15);
  or or_77 (or_77_out, or_72_out, or_56_out);
  or or_78 (or_78_out, or_68_out, or_73_out);
  or or_79 (or_79_out, or_64_out, or_57_out);
  or or_80 (or_80_out, or_49_out, or_75_out);
  or or_81 (or_81_out, or_65_out, or_70_out);
  or or_82 (or_82_out, or_66_out, or_76_out);
endmodule

module dec (
  input  A0,
  input  A1,
  input  A2,
  input  A3,
  output Y0,
  output Y1,
  output Y2,
  output Y3,
  output Y4,
  output Y5,
  output Y6,
  output Y7,
  output Y8,
  output Y9,
  output Y10,
  output Y11,
  output Y12,
  output Y13,
  output Y14,
  output Y15
);

  wire and_1_out, and_2_out, and_3_out, and_4_out, and_5_out, and_6_out, and_7_out, and_8_out, and_9_out,
       and_10_out, and_11_out, and_12_out, and_13_out, and_14_out, and_15_out, and_16_out, and_17_out,
       and_18_out, and_19_out, and_20_out, and_21_out, and_22_out, and_23_out, and_24_out, and_25_out,
       and_26_out, and_27_out, and_28_out, and_29_out, and_30_out, and_31_out, and_32_out, not_1_out,
       not_2_out, not_3_out, not_4_out, not_5_out, not_6_out, not_7_out, not_8_out, not_9_out, not_10_out,
       not_11_out;

  not not_1 (not_1_out, A0);
  not not_2 (not_2_out, A1);
  not not_3 (not_3_out, A0);
  not not_4 (not_4_out, A1);
  not not_5 (not_5_out, A0);
  not not_6 (not_6_out, A1);
  not not_7 (not_7_out, A0);
  not not_8 (not_8_out, A1);
  and and_1 (and_1_out, not_1_out, not_2_out);
  and and_2 (and_2_out, A0, not_2_out);
  and and_3 (and_3_out, not_1_out, A1);
  and and_4 (and_4_out, A1, A0);
  and and_5 (and_5_out, not_3_out, not_4_out);
  and and_6 (and_6_out, A0, not_4_out);
  and and_7 (and_7_out, not_3_out, A1);
  and and_8 (and_8_out, A1, A0);
  and and_9 (and_9_out, not_5_out, not_6_out);
  and and_10 (and_10_out, A0, not_6_out);
  and and_11 (and_11_out, not_5_out, A1);
  and and_12 (and_12_out, A1, A0);
  and and_13 (and_13_out, not_7_out, not_8_out);
  and and_14 (and_14_out, A0, not_8_out);
  and and_15 (and_15_out, not_7_out, A1);
  and and_16 (and_16_out, A1, A0);
  not not_9 (not_9_out, A2);
  not not_10 (not_10_out, A2);
  and and_17 (and_17_out, and_1_out, not_9_out);
  and and_18 (and_18_out, not_9_out, and_2_out);
  and and_19 (and_19_out, and_3_out, not_9_out);
  and and_20 (and_20_out, and_4_out, not_9_out);
  and and_21 (and_21_out, A2, and_5_out);
  and and_22 (and_22_out, A2, and_6_out);
  and and_23 (and_23_out, A2, and_7_out);
  and and_24 (and_24_out, A2, and_8_out);
  and and_25 (and_25_out, and_9_out, not_10_out);
  and and_26 (and_26_out, not_10_out, and_10_out);
  and and_27 (and_27_out, and_11_out, not_10_out);
  and and_28 (and_28_out, and_12_out, not_10_out);
  and and_29 (and_29_out, A2, and_13_out);
  and and_30 (and_30_out, A2, and_14_out);
  and and_31 (and_31_out, A2, and_15_out);
  and and_32 (and_32_out, A2, and_16_out);
  not not_11 (not_11_out, A3);
  and and_33 (Y0, not_11_out, and_17_out);
  and and_34 (Y1, not_11_out, and_18_out);
  and and_35 (Y2, not_11_out, and_19_out);
  and and_36 (Y3, not_11_out, and_20_out);
  and and_37 (Y4, not_11_out, and_21_out);
  and and_38 (Y5, not_11_out, and_22_out);
  and and_39 (Y6, not_11_out, and_23_out);
  and and_40 (Y7, not_11_out, and_24_out);
  and and_41 (Y8, A3, and_25_out);
  and and_42 (Y9, A3, and_26_out);
  and and_43 (Y10, A3, and_27_out);
  and and_44 (Y11, A3, and_28_out);
  and and_45 (Y12, A3, and_29_out);
  and and_46 (Y13, A3, and_30_out);
  and and_47 (Y14, A3, and_31_out);
  and and_48 (Y15, A3, and_32_out);
endmodule
